// Logisim project CPU.circ as structural Verilog: 3 circuits, main circuit UI
module UI (
  input  [15:0] in_1,
  input  [15:0] in_2,
  input  [15:0] in_3,
  output [15:0] out_4,
  output [15:0] out_5,
  output [15:0] out_6,
  output [15:0] out_7,
  output [15:0] out_8
);

  wire and_1_out, and_2_out, and_3_out, and_4_out, and_5_out, Clk_out, RST_out;
  wire [15:0] dispdriver_1_a, dispdriver_1_b, dispdriver_1_c, dispdriver_1_d, dispdriver_1_e, dispdriver_1_f,
       dispdriver_1_g, dispdriver_1_h, dispdriver_1_i, dispdriver_1_j, dispdriver_1_k, dispdriver_1_l,
       dispdriver_1_m, dispdriver_1_n, dispdriver_1_o, dispdriver_1_p, ram_1_data, rom_1_data;

  Clock Clk (.out(Clk_out));
  Button RST (.out(RST_out));
  CPU cpu_1 (
    .OR4(out_7), .RST(RST_out), .CLK(Clk_out), .OR2(out_5), .Dout(out_8), .OR3(out_6), .OR1(out_4),
    .IR1(in_1), .IR2(in_2), .IR3(in_3), .Exp(1'b1), .WD(1'b1), .Mo(1'b1));
  and and_1 (and_1_out, ~out_5[8], ~out_5[9], ~out_5[10]);  // AND_Gate
  ROM #(.dataWidth(16)) rom_1 (.addr(out_5[7:0]), .data(rom_1_data));
  and and_2 (and_2_out, out_5[12], and_1_out);
  DispDriver dispdriver_1 (
    .C(dispdriver_1_c), .F(dispdriver_1_f), .H(dispdriver_1_h), .A(dispdriver_1_a), .I(dispdriver_1_i),
    .E(dispdriver_1_e), .D(dispdriver_1_d), .J(dispdriver_1_j), .B(dispdriver_1_b), .G(dispdriver_1_g),
    .MemOffs(11'h200), .AddrRW(out_5), .BUSI(out_4), .Clk(Clk_out), .Rst(RST_out), .K(dispdriver_1_k),
    .L(dispdriver_1_l), .M(dispdriver_1_m), .N(dispdriver_1_n), .O(dispdriver_1_o), .P(dispdriver_1_p));
  DotMatrix #(.matrixcols(16), .matrixrows(16)) dotmatrix_1 (
    .col0(dispdriver_1_a), .col1(dispdriver_1_b), .col2(dispdriver_1_c), .col3(dispdriver_1_d),
    .col4(dispdriver_1_e), .col5(dispdriver_1_f), .col6(dispdriver_1_g), .col7(dispdriver_1_h),
    .col8(dispdriver_1_i), .col9(dispdriver_1_j), .col10(dispdriver_1_k), .col11(dispdriver_1_l),
    .col12(dispdriver_1_m), .col13(dispdriver_1_n), .col14(dispdriver_1_o), .col15(dispdriver_1_p));
  assign in_1 = and_2_out ? rom_1_data : 16'bz;  // Controlled_Buffer controlled_buffer_1
  and and_3 (and_3_out, out_5[8], ~out_5[9], ~out_5[10]);  // AND_Gate
  and and_4 (and_4_out, out_5[11], and_3_out);
  and and_5 (and_5_out, out_5[12], and_3_out);
  RAM #(.dataWidth(16), .trigger("falling")) ram_1 (
    .addr(out_5[7:0]), .we(and_4_out), .oe(and_5_out), .clk(Clk_out), .data(ram_1_data));
  assign in_1 = and_5_out ? ram_1_data : 16'bz;  // Controlled_Buffer controlled_buffer_2
  assign ram_1_data = and_4_out ? out_4 : 16'bz;  // Controlled_Buffer controlled_buffer_3

  // Notes on the sheet:
  //   contents of rom_1 (hex, n*v repeats v):
  //   8fe 1210 8ff 1104 904 7800 17fb 8fb 17fa 2903 7800 904 17fb fed 1102 7800 903 17ee 902 8000 7800 904
  //   17fb ff0 1104 7800 8f8 17f5 904 17fb 7800 8fd 17fa 70f9 904 7800 17fb 8fe 17fa 3104 7800 8ff 1100
  //   900 17fb 7800 8fb 17fa 2903 904 7800 17fb fed 1102 903 7800 17ee 902 8000 904 7800 17fb 8fe 17fa
  //   3104 7800 900 17fb ff0 1100 7800 8f6 17f5 904 17fb 7800 8ff 17fa 70f7 900 7800 17fb 8fb 17fa 2903
  //   7800 904 17fb fed 1102 7800 903 17ee 902 8000 7800 904 17fb 8fe 17fa 7800 3104 900 17fb ff0 7800
  //   1100 18fa 138*0 8 2b 20 4 0 200 20 10 1
endmodule

module CPU (
  input  Mo,
  input  CLK,
  input  Exp,
  input  RST,
  input  [15:0] IR1,
  input  [15:0] IR2,
  input  WD,
  input  [15:0] IR3,
  output [15:0] OR1,
  output [15:0] OR2,
  output [15:0] OR3,
  output [15:0] OR4,
  output [15:0] Dout
);

  wire adder_2_cout, and_1_out, and_3_out, and_4_out, and_5_out, and_6_out, and_7_out, and_8_out, and_9_out,
       and_12_out, and_13_out, and_14_out, and_15_out, and_16_out, and_17_out, and_18_out, and_19_out,
       and_20_out, and_21_out, and_22_out, and_23_out, and_24_out, and_25_out, and_26_out, and_27_out,
       and_28_out, and_29_out, and_30_out, button_1_out, CHKON, Clk_t, comparator_1_eq, comparator_2_eq,
       comparator_2_gt, comparator_2_lt, comparator_3_eq, comparator_3_gt, comparator_3_lt, comparator_4_eq,
       comparator_5_eq, comparator_6_eq, comparator_7_eq, comparator_8_eq, comparator_9_eq, comparator_10_eq,
       comparator_11_eq, comparator_12_eq, comparator_13_eq, comparator_14_eq, comparator_15_eq,
       comparator_16_eq, comparator_17_eq, comparator_18_eq, comparator_19_eq, comparator_20_eq,
       comparator_21_eq, controlled_buffer_14_out, controlled_buffer_16_out, controlled_buffer_17_out,
       counter_1_carry, counter_3_carry, counter_4_carry, d_ff_1_q, Jumpok, not_1_out, not_2_out, not_4_out,
       not_5_out, not_6_out, not_7_out, not_8_out, or_1_out, Read, Rst_t, SoftRes, subtractor_2_bout, Write;
  wire [7:0] MDO;
  wire [10:0] Addr, controlled_buffer_10_out, counter_2_q, subtractor_1_out;
  wire [15:0] adder_1_out, adder_2_out, and_10_out, Areg, Breg, controlled_buffer_7_out,
       controlled_buffer_38_out, counter_5_q, decoder_1_out0, divider_1_out, IfCR_q, IfRR_q, Input1_q,
       Input2_q, Input3_q, IntReg2_q, IntReg_q, MBUS, multiplier_1_out, negator_1_out, not_3_out, or_2_out,
       pull_resistor_2_node, ram_1_data, register_1_q, Ro1_q, Ro2_q, Ro3_q, rom_2_data, shifter_1_out,
       shifter_2_out, shifter_3_out, shifter_4_out, shifter_5_out, subtractor_2_out, xor_1_out;
  wire [15:11] controlled_buffer_10_out_2;
  wire [31:0] counter_4_q, rom_1_data;

  not not_1 (not_1_out, Clk_t);
  and and_1 (and_1_out, Write, comparator_1_eq);
  Comparator #(.width(11), .mode("unsigned")) comparator_1 (
    .a(Addr), .b(11'h7f5), .eq(comparator_1_eq));  // open: gt, lt
  Counter #(.width(3), .max('h4), .trigger("falling")) counter_1 (
    .clr(Rst_t), .load(Rst_t), .up(1'b1), .count(Clk_t), .clk(not_1_out), .carry(counter_1_carry),
    .Q(MDO[2:0]));  // open: D
  Register #(.width(16)) IfCR (.D(MBUS), .en(and_1_out), .clk(Clk_t), .Q(IfCR_q), .clr(Rst_t));
  and and_2 (Clk_t, CLK, ~rom_1_data[4]);  // AND_Gate
  Register #(.width(11)) MemPointer (.D(MBUS[10:0]), .en(rom_1_data[1]), .clk(Clk_t), .Q(Addr), .clr(Rst_t));
  Register #(.width(5)) IR (.D(MBUS[15:11]), .en(rom_1_data[0]), .clk(Clk_t), .Q(MDO[7:3]), .clr(Rst_t));
  assign Jumpok = IfCR_q[0] ? comparator_2_gt : 1'bz;  // Controlled_Buffer controlled_buffer_1
  Comparator #(.width(16)) comparator_2 (
    .a(Areg), .b(Breg), .gt(comparator_2_gt), .eq(comparator_2_eq), .lt(comparator_2_lt));
  assign Jumpok = IfCR_q[1] ? comparator_2_eq : 1'bz;  // Controlled_Buffer controlled_buffer_2
  assign Jumpok = IfCR_q[2] ? comparator_2_lt : 1'bz;  // Controlled_Buffer controlled_buffer_3
  Pull_Resistor pull_resistor_1 (.node(Jumpok));
  assign Jumpok = IfCR_q[3] ? comparator_3_gt : 1'bz;  // Controlled_Buffer controlled_buffer_4
  assign Jumpok = IfCR_q[4] ? comparator_3_eq : 1'bz;  // Controlled_Buffer controlled_buffer_5
  Comparator #(.width(16), .mode("unsigned")) comparator_3 (
    .a(Areg), .b(Breg), .gt(comparator_3_gt), .eq(comparator_3_eq), .lt(comparator_3_lt));
  assign Jumpok = IfCR_q[5] ? comparator_3_lt : 1'bz;  // Controlled_Buffer controlled_buffer_6
  ROM #(.dataWidth(32)) rom_1 (
    .addr(MDO), .data({rom_1_data[31], CHKON, rom_1_data[29:4], Write, Read, rom_1_data[1:0]}));
  Comparator #(.width(11), .mode("unsigned")) comparator_4 (
    .a(Addr), .b(11'h7f4), .eq(comparator_4_eq));  // open: gt, lt
  not not_2 (not_2_out, Jumpok);
  assign controlled_buffer_7_out = Jumpok ? {16{1'b1}} : 16'bz;  // Controlled_Buffer controlled_buffer_7
  assign controlled_buffer_7_out = not_2_out ? {16{1'b0}} : 16'bz;  // Controlled_Buffer controlled_buffer_8
  and and_3 (and_3_out, Read, comparator_4_eq);
  Register #(.width(16)) IfRR (.D(controlled_buffer_7_out), .en(1'b1), .clk(counter_1_carry), .Q(IfRR_q), .clr(Rst_t));
  Subtractor #(.width(11)) subtractor_1 (
    .a(controlled_buffer_10_out), .b(11'h1), .out(subtractor_1_out));  // open: bin, bout
  and and_4 (and_4_out, Clk_t, ~CHKON, rom_1_data[21]);  // AND_Gate
  and and_5 (and_5_out, Clk_t, rom_1_data[21], Jumpok, CHKON);
  assign MBUS = and_3_out ? IfRR_q : 16'bz;  // Controlled_Buffer controlled_buffer_9
  Counter #(.width(11), .max('h7ff)) counter_2 (
    .clr(Rst_t), .load(rom_1_data[21]), .count(counter_1_carry), .clk(or_1_out), .D(subtractor_1_out),
    .Q(counter_2_q));  // open: up, carry
  assign {controlled_buffer_10_out_2, controlled_buffer_10_out} = rom_1_data[21] ? MBUS : 16'bz;  // Controlled_Buffer controlled_buffer_10
  or or_1 (or_1_out, counter_1_carry, and_5_out, and_4_out);
  and and_6 (and_6_out, Write, comparator_5_eq);
  Comparator #(.width(11), .mode("unsigned")) comparator_5 (
    .a(Addr), .b(11'h7fb), .eq(comparator_5_eq));  // open: gt, lt
  and and_7 (and_7_out, Write, comparator_6_eq);
  Comparator #(.width(11), .mode("unsigned")) comparator_6 (
    .a(Addr), .b(11'h7fa), .eq(comparator_6_eq));  // open: gt, lt
  Comparator #(.width(11), .mode("unsigned")) comparator_7 (
    .a(Addr), .b(11'h7ef), .eq(comparator_7_eq));  // open: gt, lt
  Register #(.width(16)) RegA (.D(MBUS), .en(and_6_out), .clk(Clk_t), .Q(Areg), .clr(Rst_t));
  Register #(.width(16)) RegB (.D(MBUS), .en(and_7_out), .clk(Clk_t), .Q(Breg), .clr(Rst_t));
  assign MBUS = rom_1_data[22] ? {{5{1'b0}}, counter_2_q} : 16'bz;  // Controlled_Buffer controlled_buffer_11
  Counter #(.width(5), .max('h1f)) counter_3 (
    .clr(rom_1_data[31]), .count(CLK), .clk(CLK), .carry(counter_3_carry));  // open: load, up, D, Q
  and and_8 (and_8_out, Write, comparator_7_eq);
  Register #(.width(16)) IntReg (.D(MBUS), .en(rom_1_data[17]), .clk(Clk_t), .Q(IntReg_q), .clr(Rst_t));
  Register #(.width(16)) register_1 (.D(MBUS), .en(and_8_out), .clk(Clk_t), .Q(register_1_q), .clr(Rst_t));
  Comparator #(.width(11), .mode("unsigned")) comparator_8 (
    .a(Addr), .b(11'h7f0), .eq(comparator_8_eq));  // open: gt, lt
  assign MBUS = rom_1_data[18] ? IntReg_q : 16'bz;  // Controlled_Buffer controlled_buffer_12
  and and_9 (and_9_out, Read, comparator_8_eq);
  Adder #(.width(16)) adder_1 (.a(Areg), .b(16'h1), .out(adder_1_out));  // open: cin, cout
  assign MBUS = and_9_out ? adder_1_out : 16'bz;  // Controlled_Buffer controlled_buffer_13
  assign controlled_buffer_14_out = rom_1_data[19] ? d_ff_1_q : 1'bz;  // Controlled_Buffer controlled_buffer_14
  assign MBUS = rom_1_data[16] ? adder_2_out : 16'bz;  // Controlled_Buffer controlled_buffer_15
  Adder #(.width(16)) adder_2 (
    .a(Areg), .b(Breg), .out(adder_2_out), .cin(controlled_buffer_14_out), .cout(adder_2_cout));
  assign controlled_buffer_16_out = rom_1_data[20] ? adder_2_cout : 1'bz;  // Controlled_Buffer controlled_buffer_16
  assign controlled_buffer_17_out = rom_1_data[19] ? d_ff_1_q : 1'bz;  // Controlled_Buffer controlled_buffer_17
  assign MBUS = rom_1_data[15] ? subtractor_2_out : 16'bz;  // Controlled_Buffer controlled_buffer_18
  Subtractor #(.width(16)) subtractor_2 (
    .a(Areg), .b(Breg), .out(subtractor_2_out), .bin(controlled_buffer_17_out), .bout(subtractor_2_bout));
  assign controlled_buffer_16_out = rom_1_data[20] ? subtractor_2_bout : 1'bz;  // Controlled_Buffer controlled_buffer_19
  assign MBUS = rom_1_data[14] ? multiplier_1_out : 16'bz;  // Controlled_Buffer controlled_buffer_20
  Multiplier #(.width(16)) multiplier_1 (.a(Areg), .b(Breg), .out(multiplier_1_out));  // open: cin, cout
  Divider #(.width(16)) divider_1 (.a(Areg), .b(Breg), .out(divider_1_out));  // open: upper, rem
  assign MBUS = rom_1_data[13] ? divider_1_out : 16'bz;  // Controlled_Buffer controlled_buffer_21
  Negator #(.width(16)) negator_1 (.in(Areg), .out(negator_1_out));
  assign MBUS = rom_1_data[12] ? negator_1_out : 16'bz;  // Controlled_Buffer controlled_buffer_22
  Shifter #(.width(16)) shifter_1 (.in(Areg), .\dist (Breg[3:0]), .out(shifter_1_out));
  assign MBUS = rom_1_data[11] ? shifter_1_out : 16'bz;  // Controlled_Buffer controlled_buffer_23
  assign MBUS = rom_1_data[10] ? shifter_2_out : 16'bz;  // Controlled_Buffer controlled_buffer_24
  Shifter #(.width(16), .shift("lr")) shifter_2 (.in(Areg), .\dist (Breg[3:0]), .out(shifter_2_out));
  assign MBUS = rom_1_data[9] ? shifter_3_out : 16'bz;  // Controlled_Buffer controlled_buffer_25
  Shifter #(.width(16), .shift("ar")) shifter_3 (.in(Areg), .\dist (Breg[3:0]), .out(shifter_3_out));
  assign MBUS = rom_1_data[8] ? shifter_4_out : 16'bz;  // Controlled_Buffer controlled_buffer_26
  Shifter #(.width(16), .shift("rl")) shifter_4 (.in(Areg), .\dist (Breg[3:0]), .out(shifter_4_out));
  assign MBUS = rom_1_data[7] ? shifter_5_out : 16'bz;  // Controlled_Buffer controlled_buffer_27
  Shifter #(.width(16), .shift("rr")) shifter_5 (.in(Areg), .\dist (Breg[3:0]), .out(shifter_5_out));
  assign MBUS = rom_1_data[5] ? and_10_out : 16'bz;  // Controlled_Buffer controlled_buffer_28
  assign and_10_out = Areg & Breg;  // AND_Gate and_10, 16 bits wide
  assign or_2_out = Areg | Breg;  // OR_Gate or_2, 16 bits wide
  assign MBUS = rom_1_data[6] ? or_2_out : 16'bz;  // Controlled_Buffer controlled_buffer_29
  assign not_3_out = ~Areg;  // NOT_Gate not_3, 16 bits wide
  assign MBUS = rom_1_data[28] ? not_3_out : 16'bz;  // Controlled_Buffer controlled_buffer_30
  assign MBUS = rom_1_data[29] ? xor_1_out : 16'bz;  // Controlled_Buffer controlled_buffer_31
  assign xor_1_out = Areg ^ Breg;  // XOR_Gate xor_1, 16 bits wide
  and and_11 (SoftRes, WD, ~register_1_q[0], counter_3_carry);  // AND_Gate
  D_Flip_Flop d_ff_1 (.D(controlled_buffer_16_out), .clk(and_12_out), .Q(d_ff_1_q));  // open: Qn, preset, reset
  and and_12 (and_12_out, Clk_t, rom_1_data[20]);
  Comparator #(.width(11), .mode("unsigned")) comparator_9 (
    .a(Addr), .b(11'h7ed), .eq(comparator_9_eq));  // open: gt, lt
  Register #(.width(16)) IntReg2 (.D(MBUS), .en(and_13_out), .clk(Clk_t), .Q(IntReg2_q), .clr(Rst_t));
  and and_13 (and_13_out, Write, comparator_10_eq);
  Comparator #(.width(11), .mode("unsigned")) comparator_10 (
    .a(Addr), .b(11'h7ee), .eq(comparator_10_eq));  // open: gt, lt
  and and_14 (and_14_out, Read, comparator_9_eq);
  Decoder #(.select(4)) decoder_1 (
    .out0(decoder_1_out0[0]), .out1(decoder_1_out0[1]), .out2(decoder_1_out0[2]), .out3(decoder_1_out0[3]),
    .out4(decoder_1_out0[4]), .out5(decoder_1_out0[5]), .out6(decoder_1_out0[6]), .out7(decoder_1_out0[7]),
    .out8(decoder_1_out0[8]), .out9(decoder_1_out0[9]), .out10(decoder_1_out0[10]),
    .out11(decoder_1_out0[11]), .out12(decoder_1_out0[12]), .out13(decoder_1_out0[13]),
    .out14(decoder_1_out0[14]), .out15(decoder_1_out0[15]), .sel(Areg[3:0]));  // open: en
  and and_15 (and_15_out, ~Addr[8], ~Addr[9], ~Addr[10]);  // AND_Gate
  ROM #(.dataWidth(16)) rom_2 (.addr(Addr[7:0]), .data(rom_2_data));
  assign MBUS = rom_1_data[24] ? IntReg2_q : 16'bz;  // Controlled_Buffer controlled_buffer_32
  assign MBUS = and_14_out ? decoder_1_out0 : 16'bz;  // Controlled_Buffer controlled_buffer_33
  Counter #(.width(32), .max('hffffffff)) counter_4 (
    .clr(Rst_t), .count(Clk_t), .clk(Clk_t), .carry(counter_4_carry), .Q(counter_4_q));  // open: load, up, D
  not not_4 (not_4_out, Mo);
  and and_16 (and_16_out, Read, not_4_out, and_15_out);
  Comparator #(.width(11), .mode("unsigned")) comparator_11 (
    .a(Addr), .b(11'h7f9), .eq(comparator_11_eq));  // open: gt, lt
  Comparator #(.width(11), .mode("unsigned")) comparator_12 (
    .a(Addr), .b(11'h7f8), .eq(comparator_12_eq));  // open: gt, lt
  Comparator #(.width(11), .mode("unsigned")) comparator_13 (
    .a(Addr), .b(11'h7f7), .eq(comparator_13_eq));  // open: gt, lt
  Comparator #(.width(11), .mode("unsigned")) comparator_14 (
    .a(Addr), .b(11'h7f6), .eq(comparator_14_eq));  // open: gt, lt
  Comparator #(.width(11), .mode("unsigned")) comparator_15 (
    .a(Addr), .b({11{1'b1}}), .eq(comparator_15_eq));  // open: gt, lt
  Comparator #(.width(11), .mode("unsigned")) comparator_16 (
    .a(Addr), .b(11'h7fe), .eq(comparator_16_eq));  // open: gt, lt
  Comparator #(.width(11), .mode("unsigned")) comparator_17 (
    .a(Addr), .b(11'h7fd), .eq(comparator_17_eq));  // open: gt, lt
  Comparator #(.width(11), .mode("unsigned")) comparator_18 (
    .a(Addr), .b(11'h7fc), .eq(comparator_18_eq));  // open: gt, lt
  and and_17 (and_17_out, Write, comparator_11_eq);
  and and_18 (and_18_out, Write, comparator_12_eq);
  and and_19 (and_19_out, Write, comparator_13_eq);
  and and_20 (and_20_out, Write, comparator_14_eq);
  and and_21 (and_21_out, Write, comparator_15_eq);
  and and_22 (and_22_out, Read, comparator_16_eq);
  and and_23 (and_23_out, Read, comparator_17_eq);
  and and_24 (and_24_out, Read, comparator_18_eq);
  assign MBUS = and_16_out ? rom_2_data : 16'bz;  // Controlled_Buffer controlled_buffer_34
  Register #(.width(16)) Ro1 (.D(MBUS), .en(and_17_out), .clk(Clk_t), .Q(Ro1_q), .clr(Rst_t));
  Register #(.width(16)) Ro2 (.D(MBUS), .en(and_18_out), .clk(Clk_t), .Q(Ro2_q), .clr(Rst_t));
  Register #(.width(16)) Ro3 (.D(MBUS), .en(and_19_out), .clk(Clk_t), .Q(Ro3_q), .clr(Rst_t));
  Register #(.width(16)) Ro4 (.D(MBUS), .en(and_20_out), .clk(Clk_t), .Q(OR4), .clr(Rst_t));
  Register #(.width(16)) DISP (.D(MBUS), .en(and_21_out), .clk(Clk_t), .Q(Dout), .clr(Rst_t));
  Register #(.width(16)) Input1 (
    .D(controlled_buffer_38_out), .en(1'b1), .clk(counter_1_carry), .Q(Input1_q), .clr(Rst_t));
  Register #(.width(16)) Input2 (.D(IR2), .en(1'b1), .clk(counter_1_carry), .Q(Input2_q), .clr(Rst_t));
  Register #(.width(16)) Input3 (.D(IR3), .en(1'b1), .clk(counter_1_carry), .Q(Input3_q), .clr(Rst_t));
  assign MBUS = and_22_out ? Input1_q : 16'bz;  // Controlled_Buffer controlled_buffer_35
  assign MBUS = and_23_out ? Input2_q : 16'bz;  // Controlled_Buffer controlled_buffer_36
  assign MBUS = and_24_out ? Input3_q : 16'bz;  // Controlled_Buffer controlled_buffer_37
  Counter #(.width(16), .max('hffff)) counter_5 (
    .clr(Rst_t), .count(counter_4_carry), .clk(counter_4_carry), .Q(counter_5_q));  // open: load, up, D, carry
  Hex_Digit_Display hex_digit_display_1 (.value(Dout[11:8]));  // open: dp
  Hex_Digit_Display hex_digit_display_2 (.value(Dout[15:12]));  // open: dp
  and and_25 (and_25_out, Read, comparator_19_eq);
  Comparator #(.width(11), .mode("unsigned")) comparator_19 (
    .a(Addr), .b(11'h7f3), .eq(comparator_19_eq));  // open: gt, lt
  and and_26 (and_26_out, Read, comparator_20_eq);
  Comparator #(.width(11), .mode("unsigned")) comparator_20 (
    .a(Addr), .b(11'h7f2), .eq(comparator_20_eq));  // open: gt, lt
  and and_27 (and_27_out, Read, comparator_21_eq);
  Comparator #(.width(11), .mode("unsigned")) comparator_21 (
    .a(Addr), .b(11'h7f1), .eq(comparator_21_eq));  // open: gt, lt
  and and_28 (and_28_out, Addr[8], ~Addr[9], ~Addr[10]);  // AND_Gate
  Hex_Digit_Display hex_digit_display_3 (.value(Dout[3:0]));  // open: dp
  Hex_Digit_Display hex_digit_display_4 (.value(Dout[7:4]));  // open: dp
  assign controlled_buffer_38_out = Exp ? pull_resistor_2_node : 16'bz;  // Controlled_Buffer controlled_buffer_38
  Pull_Resistor pull_resistor_2 (.node(pull_resistor_2_node));
  assign controlled_buffer_38_out = not_5_out ? IR1 : 16'bz;  // Controlled_Buffer controlled_buffer_39
  assign MBUS = Exp ? IR1 : 16'bz;  // Controlled_Buffer controlled_buffer_40
  and and_29 (and_29_out, Write, not_4_out, and_28_out);
  and and_30 (and_30_out, Read, not_4_out, and_28_out);
  or or_3 (Rst_t, RST, SoftRes, button_1_out);
  Button button_1 (.out(button_1_out));
  not not_5 (not_5_out, Exp);
  assign MBUS = and_25_out ? counter_4_q[15:0] : 16'bz;  // Controlled_Buffer controlled_buffer_41
  assign MBUS = and_26_out ? counter_4_q[31:16] : 16'bz;  // Controlled_Buffer controlled_buffer_42
  assign MBUS = and_27_out ? counter_5_q : 16'bz;  // Controlled_Buffer controlled_buffer_43
  RAM #(.dataWidth(16), .trigger("falling")) ram_1 (
    .addr(Addr[7:0]), .we(and_29_out), .oe(and_30_out), .clk(CLK), .data(ram_1_data));
  not not_6 (not_6_out, Exp);
  assign OR1 = not_6_out ? Ro1_q : 16'bz;  // Controlled_Buffer controlled_buffer_44
  assign OR1 = Exp ? MBUS : 16'bz;  // Controlled_Buffer controlled_buffer_45
  not not_7 (not_7_out, Exp);
  assign OR2 = not_7_out ? Ro2_q : 16'bz;  // Controlled_Buffer controlled_buffer_46
  assign OR2 = Exp ? {Ro2_q[15:13], Read, Write, Addr} : 16'bz;  // Controlled_Buffer controlled_buffer_47
  not not_8 (not_8_out, Exp);
  assign OR3 = not_8_out ? Ro3_q : 16'bz;  // Controlled_Buffer controlled_buffer_48
  assign OR3 = Exp ? {Ro3_q[15:8], MDO} : 16'bz;  // Controlled_Buffer controlled_buffer_49
  assign ram_1_data = and_29_out ? MBUS : 16'bz;  // Controlled_Buffer controlled_buffer_50
  assign MBUS = and_30_out ? ram_1_data : 16'bz;  // Controlled_Buffer controlled_buffer_51

  // Other names for the same wires on the sheet: ClkI = CLK

  // Notes on the sheet:
  //   contents of rom_1 (hex, n*v repeats v):
  //   400002 7 6*0 400002 7 20004 5*0 400002 7 40008 5*0 400002 7 200004 5*0 400002 7 10 5*0 400002 7
  //   10008 5*0 400002 7 8008 5*0 400002 7 2008 5*0 400002 7 4008 5*0 400002 7 1008 5*0 400002 7 28 5*0
  //   400002 7 48 5*0 400002 7 10000008 5*0 400002 7 20000008 5*0 400002 7 40200004 5*0 400002 7 80000000
  //   5*0 400002 7 1000002 40008 4*0 400002 7 6*0 400002 7 6*0 400002 7 6*0 400002 7 6*0 400002 7 6*0
  //   400002 7 6*0 400002 7 6*0 400002 7 6*0 400002 7 6*0 400002 7 6*0 400002 7 6*0 400002 7 6*0 400002 7
  //   6*0 400002 7 6*0 400002 7
  //   contents of rom_2 (hex, n*v repeats v):
  //   8ff 1100 900 17fb ff0 7800 1100 900 17ff 8fb 7800 17f5 900 17fb 8fe 7800 17fa 70fc 8ff 1100 7800
  //   18fd 229*0 20 2 2 1f
endmodule

module DispDriver (
  input  Rst,
  input  Clk,
  input  [15:0] BUSI,
  input  [15:0] AddrRW,
  input  [10:0] MemOffs,
  output [15:0] A,
  output [15:0] B,
  output [15:0] C,
  output [15:0] D,
  output [15:0] E,
  output [15:0] F,
  output [15:0] G,
  output [15:0] H,
  output [15:0] I,
  output [15:0] J,
  output [15:0] K,
  output [15:0] L,
  output [15:0] M,
  output [15:0] N,
  output [15:0] O,
  output [15:0] P
);

  wire and_1_out, and_2_out, and_3_out, and_4_out, and_5_out, and_6_out, and_7_out, and_8_out, and_9_out,
       and_10_out, and_11_out, and_12_out, and_13_out, and_14_out, and_15_out, and_16_out, and_17_out,
       comparator_1_eq, comparator_2_eq, comparator_3_eq, comparator_4_eq, comparator_5_eq, comparator_6_eq,
       comparator_7_eq, comparator_8_eq, comparator_9_eq, comparator_10_eq, comparator_11_eq,
       comparator_12_eq, comparator_13_eq, comparator_14_eq, comparator_15_eq, comparator_16_eq,
       comparator_17_eq;
  wire [10:0] adder_1_out, adder_2_out, adder_3_out, adder_4_out, adder_5_out, adder_6_out, adder_7_out,
       adder_8_out, adder_9_out, adder_10_out, adder_11_out, adder_12_out, adder_13_out, adder_14_out,
       adder_15_out, adder_16_out, adder_17_out;
  wire [15:0] register_1_q, register_2_q, register_3_q, register_4_q, register_5_q, register_6_q,
       register_7_q, register_8_q, register_9_q, register_10_q, register_11_q, register_12_q, register_13_q,
       register_14_q, register_15_q, register_16_q, register_17_q;

  Adder #(.width(11)) adder_1 (.a(MemOffs), .b({11{1'b0}}), .out(adder_1_out));  // open: cin, cout
  Adder #(.width(11)) adder_2 (.a(MemOffs), .b(11'h1), .out(adder_2_out));  // open: cin, cout
  Adder #(.width(11)) adder_3 (.a(MemOffs), .b(11'h2), .out(adder_3_out));  // open: cin, cout
  Adder #(.width(11)) adder_4 (.a(MemOffs), .b(11'h3), .out(adder_4_out));  // open: cin, cout
  Adder #(.width(11)) adder_5 (.a(MemOffs), .b(11'h4), .out(adder_5_out));  // open: cin, cout
  Adder #(.width(11)) adder_6 (.a(MemOffs), .b(11'h5), .out(adder_6_out));  // open: cin, cout
  Adder #(.width(11)) adder_7 (.a(MemOffs), .b(11'h6), .out(adder_7_out));  // open: cin, cout
  Adder #(.width(11)) adder_8 (.a(MemOffs), .b(11'h7), .out(adder_8_out));  // open: cin, cout
  Adder #(.width(11)) adder_9 (.a(MemOffs), .b(11'h8), .out(adder_9_out));  // open: cin, cout
  Adder #(.width(11)) adder_10 (.a(MemOffs), .b(11'h9), .out(adder_10_out));  // open: cin, cout
  Adder #(.width(11)) adder_11 (.a(MemOffs), .b(11'ha), .out(adder_11_out));  // open: cin, cout
  Adder #(.width(11)) adder_12 (.a(MemOffs), .b(11'hb), .out(adder_12_out));  // open: cin, cout
  Adder #(.width(11)) adder_13 (.a(MemOffs), .b(11'hc), .out(adder_13_out));  // open: cin, cout
  Adder #(.width(11)) adder_14 (.a(MemOffs), .b(11'hd), .out(adder_14_out));  // open: cin, cout
  Adder #(.width(11)) adder_15 (.a(MemOffs), .b(11'he), .out(adder_15_out));  // open: cin, cout
  Adder #(.width(11)) adder_16 (.a(MemOffs), .b(11'hf), .out(adder_16_out));  // open: cin, cout
  Adder #(.width(11)) adder_17 (.a(MemOffs), .b(11'h10), .out(adder_17_out));  // open: cin, cout
  Comparator #(.width(11), .mode("unsigned")) comparator_1 (
    .a(adder_1_out), .b(AddrRW[10:0]), .eq(comparator_1_eq));  // open: gt, lt
  Comparator #(.width(11), .mode("unsigned")) comparator_2 (
    .a(adder_2_out), .b(AddrRW[10:0]), .eq(comparator_2_eq));  // open: gt, lt
  Comparator #(.width(11), .mode("unsigned")) comparator_3 (
    .a(adder_3_out), .b(AddrRW[10:0]), .eq(comparator_3_eq));  // open: gt, lt
  Comparator #(.width(11), .mode("unsigned")) comparator_4 (
    .a(adder_4_out), .b(AddrRW[10:0]), .eq(comparator_4_eq));  // open: gt, lt
  Comparator #(.width(11), .mode("unsigned")) comparator_5 (
    .a(adder_5_out), .b(AddrRW[10:0]), .eq(comparator_5_eq));  // open: gt, lt
  Comparator #(.width(11), .mode("unsigned")) comparator_6 (
    .a(adder_6_out), .b(AddrRW[10:0]), .eq(comparator_6_eq));  // open: gt, lt
  Comparator #(.width(11), .mode("unsigned")) comparator_7 (
    .a(adder_7_out), .b(AddrRW[10:0]), .eq(comparator_7_eq));  // open: gt, lt
  Comparator #(.width(11), .mode("unsigned")) comparator_8 (
    .a(adder_8_out), .b(AddrRW[10:0]), .eq(comparator_8_eq));  // open: gt, lt
  Comparator #(.width(11), .mode("unsigned")) comparator_9 (
    .a(adder_9_out), .b(AddrRW[10:0]), .eq(comparator_9_eq));  // open: gt, lt
  Comparator #(.width(11), .mode("unsigned")) comparator_10 (
    .a(adder_10_out), .b(AddrRW[10:0]), .eq(comparator_10_eq));  // open: gt, lt
  Comparator #(.width(11), .mode("unsigned")) comparator_11 (
    .a(adder_11_out), .b(AddrRW[10:0]), .eq(comparator_11_eq));  // open: gt, lt
  Comparator #(.width(11), .mode("unsigned")) comparator_12 (
    .a(adder_12_out), .b(AddrRW[10:0]), .eq(comparator_12_eq));  // open: gt, lt
  Comparator #(.width(11), .mode("unsigned")) comparator_13 (
    .a(adder_13_out), .b(AddrRW[10:0]), .eq(comparator_13_eq));  // open: gt, lt
  Comparator #(.width(11), .mode("unsigned")) comparator_14 (
    .a(adder_14_out), .b(AddrRW[10:0]), .eq(comparator_14_eq));  // open: gt, lt
  Comparator #(.width(11), .mode("unsigned")) comparator_15 (
    .a(adder_15_out), .b(AddrRW[10:0]), .eq(comparator_15_eq));  // open: gt, lt
  Comparator #(.width(11), .mode("unsigned")) comparator_16 (
    .a(adder_16_out), .b(AddrRW[10:0]), .eq(comparator_16_eq));  // open: gt, lt
  Comparator #(.width(11), .mode("unsigned")) comparator_17 (
    .a(adder_17_out), .b(AddrRW[10:0]), .eq(comparator_17_eq));  // open: gt, lt
  Register #(.width(16)) register_1 (.D(BUSI), .en(and_1_out), .clk(Clk), .Q(register_1_q), .clr(Rst));
  and and_1 (and_1_out, AddrRW[11], comparator_1_eq);
  Register #(.width(16)) register_2 (.D(BUSI), .en(and_2_out), .clk(Clk), .Q(register_2_q), .clr(Rst));
  and and_2 (and_2_out, AddrRW[11], comparator_2_eq);
  Register #(.width(16)) register_3 (.D(BUSI), .en(and_3_out), .clk(Clk), .Q(register_3_q), .clr(Rst));
  and and_3 (and_3_out, AddrRW[11], comparator_3_eq);
  Register #(.width(16)) register_4 (.D(BUSI), .en(and_4_out), .clk(Clk), .Q(register_4_q), .clr(Rst));
  and and_4 (and_4_out, AddrRW[11], comparator_4_eq);
  Register #(.width(16)) register_5 (.D(BUSI), .en(and_5_out), .clk(Clk), .Q(register_5_q), .clr(Rst));
  and and_5 (and_5_out, AddrRW[11], comparator_5_eq);
  Register #(.width(16)) register_6 (.D(BUSI), .en(and_6_out), .clk(Clk), .Q(register_6_q), .clr(Rst));
  and and_6 (and_6_out, AddrRW[11], comparator_6_eq);
  Register #(.width(16)) register_7 (.D(BUSI), .en(and_7_out), .clk(Clk), .Q(register_7_q), .clr(Rst));
  and and_7 (and_7_out, AddrRW[11], comparator_7_eq);
  Register #(.width(16)) register_8 (.D(BUSI), .en(and_8_out), .clk(Clk), .Q(register_8_q), .clr(Rst));
  and and_8 (and_8_out, AddrRW[11], comparator_8_eq);
  Register #(.width(16)) register_9 (.D(BUSI), .en(and_9_out), .clk(Clk), .Q(register_9_q), .clr(Rst));
  and and_9 (and_9_out, AddrRW[11], comparator_9_eq);
  Register #(.width(16)) register_10 (.D(BUSI), .en(and_10_out), .clk(Clk), .Q(register_10_q), .clr(Rst));
  and and_10 (and_10_out, AddrRW[11], comparator_10_eq);
  Register #(.width(16)) register_11 (.D(BUSI), .en(and_11_out), .clk(Clk), .Q(register_11_q), .clr(Rst));
  and and_11 (and_11_out, AddrRW[11], comparator_11_eq);
  Register #(.width(16)) register_12 (.D(BUSI), .en(and_12_out), .clk(Clk), .Q(register_12_q), .clr(Rst));
  and and_12 (and_12_out, AddrRW[11], comparator_12_eq);
  Register #(.width(16)) register_13 (.D(BUSI), .en(and_13_out), .clk(Clk), .Q(register_13_q), .clr(Rst));
  and and_13 (and_13_out, AddrRW[11], comparator_13_eq);
  Register #(.width(16)) register_14 (.D(BUSI), .en(and_14_out), .clk(Clk), .Q(register_14_q), .clr(Rst));
  and and_14 (and_14_out, AddrRW[11], comparator_14_eq);
  Register #(.width(16)) register_15 (.D(BUSI), .en(and_15_out), .clk(Clk), .Q(register_15_q), .clr(Rst));
  and and_15 (and_15_out, AddrRW[11], comparator_15_eq);
  Register #(.width(16)) register_16 (.D(BUSI), .en(and_16_out), .clk(Clk), .Q(register_16_q), .clr(Rst));
  and and_16 (and_16_out, AddrRW[11], comparator_16_eq);
  Register #(.width(16)) register_17 (.D(BUSI), .en(and_17_out), .clk(Clk), .Q(register_17_q), .clr(Rst));
  and and_17 (and_17_out, AddrRW[11], comparator_17_eq);
  Pull_Resistor pull_resistor_1 (.node(A));
  assign A = register_17_q[0] ? register_1_q : 16'bz;  // Controlled_Buffer controlled_buffer_1
  Pull_Resistor pull_resistor_2 (.node(B));
  assign B = register_17_q[0] ? register_2_q : 16'bz;  // Controlled_Buffer controlled_buffer_2
  assign C = register_17_q[0] ? register_3_q : 16'bz;  // Controlled_Buffer controlled_buffer_3
  Pull_Resistor pull_resistor_3 (.node(C));
  assign D = register_17_q[0] ? register_4_q : 16'bz;  // Controlled_Buffer controlled_buffer_4
  Pull_Resistor pull_resistor_4 (.node(D));
  assign E = register_17_q[0] ? register_5_q : 16'bz;  // Controlled_Buffer controlled_buffer_5
  Pull_Resistor pull_resistor_5 (.node(E));
  assign F = register_17_q[0] ? register_6_q : 16'bz;  // Controlled_Buffer controlled_buffer_6
  Pull_Resistor pull_resistor_6 (.node(F));
  assign G = register_17_q[0] ? register_7_q : 16'bz;  // Controlled_Buffer controlled_buffer_7
  Pull_Resistor pull_resistor_7 (.node(G));
  assign H = register_17_q[0] ? register_8_q : 16'bz;  // Controlled_Buffer controlled_buffer_8
  Pull_Resistor pull_resistor_8 (.node(H));
  assign I = register_17_q[0] ? register_9_q : 16'bz;  // Controlled_Buffer controlled_buffer_9
  Pull_Resistor pull_resistor_9 (.node(I));
  Pull_Resistor pull_resistor_10 (.node(J));
  assign J = register_17_q[0] ? register_10_q : 16'bz;  // Controlled_Buffer controlled_buffer_10
  assign K = register_17_q[0] ? register_11_q : 16'bz;  // Controlled_Buffer controlled_buffer_11
  Pull_Resistor pull_resistor_11 (.node(K));
  assign L = register_17_q[0] ? register_12_q : 16'bz;  // Controlled_Buffer controlled_buffer_12
  Pull_Resistor pull_resistor_12 (.node(L));
  Pull_Resistor pull_resistor_13 (.node(M));
  assign M = register_17_q[0] ? register_13_q : 16'bz;  // Controlled_Buffer controlled_buffer_13
  assign N = register_17_q[0] ? register_14_q : 16'bz;  // Controlled_Buffer controlled_buffer_14
  Pull_Resistor pull_resistor_14 (.node(N));
  Pull_Resistor pull_resistor_15 (.node(O));
  assign O = register_17_q[0] ? register_15_q : 16'bz;  // Controlled_Buffer controlled_buffer_15
  assign P = register_17_q[0] ? register_16_q : 16'bz;  // Controlled_Buffer controlled_buffer_16
  Pull_Resistor pull_resistor_16 (.node(P));

  // Other names for the same wires on the sheet: Addr[10:0] = AddrRW[10:0]; Wr = AddrRW[11]; IntBus[15:0] = BUSI;
  //   MO[10:0] = MemOffs
endmodule
